# Fritzing sketch sketch_pcb (saved by Fritzing 0.9.3b)

parts:
  U1 = ESP8266 NodeMCU LoLin module
  DHT1 = DHT22 Humidity and Temperature Sensor
  Grove1 = Grove OLED 128x96
  Grove2 = Grove OLED 128x96
  Componente1 = Real Time Clock Module - DS1307 RTC Breakout Board
  S3 = Toggle Switch [package=THT]
  U2 = POT [package=3362u]
  S2 = SWITCH-MOMENTARY-2 [package=tactile-switch-1101ne]
  S1 = SWITCH-MOMENTARY-2 [package=tactile-switch-1101ne]
  U3 = RELAY-SOLIDSTATE [package=relay-s108t02]
  U4 = RELAY-SOLIDSTATE [package=relay-s108t02]
  U5 = RELAY-SOLIDSTATE [package=relay-s108t02]
  1k_FRIO = 220 Ω Resistor [package=THT]
  10k_FRIO = 220 Ω Resistor [package=THT]
  NPN_FRIO = npn-Powertransistor [package="TO220 [THT]"]
  100nF_SSR_FRIO = Ceramic Capacitor [package="100 mil [THT, multilayer]"]
  1k_CALOR = 220 Ω Resistor [package=THT]
  10k_CALOR = 220 Ω Resistor [package=THT]
  NPN_CALOR = npn-Powertransistor [package="TO220 [THT]"]
  100nF_SSR_CALOR = Ceramic Capacitor [package="100 mil [THT, multilayer]"]
  1k_VENT = 220 Ω Resistor [package=THT]
  10k_VENT = 220 Ω Resistor [package=THT]
  NPN_VENT = npn-Powertransistor [package="TO220 [THT]"]
  100nF_SSR_VENT = Ceramic Capacitor [package="100 mil [THT, multilayer]"]
  100nF_ESP8266 = Ceramic Capacitor [package="100 mil [THT, multilayer]"]
  100nF_OLED_A = Ceramic Capacitor [package="100 mil [THT, multilayer]"]
  100nF_OLED_B = Ceramic Capacitor [package="100 mil [THT, multilayer]"]
  100nF_RTC = Ceramic Capacitor [package="100 mil [THT, multilayer]"]
  100nF_DHT22 = Ceramic Capacitor [package="100 mil [THT, multilayer]"]
  100uF_bulk_3V3 = Electrolytic Capacitor [package="100 mil [THT, electrolytic]"]
  4_7k_SDA = 220 Ω Resistor [package=THT]
  4_7k_SCL = 220 Ω Resistor [package=THT]

nets:
  N1: U1.D0, S3.COM
  N2: U1.D1, Grove1.SCL, Grove2.SCL, Componente1.SCL, 4_7k_SCL.Pin_0
  N3: U1.D2, Grove1.SDA, Grove2.SDA, Componente1.SDA, 4_7k_SDA.Pin_0
  N4: U1.D3, S2.2
  N5: U1.D4, S1.2
  VCC: U1.3V3, DHT1.VDD, Grove1.VCC, Grove2.VCC, Componente1.5V, S3.L2, U2.A, 100nF_ESP8266.0, 100nF_OLED_A.0, 100nF_OLED_B.0, 100nF_RTC.0, 100nF_DHT22.0, 100uF_bulk_3V3.+, 4_7k_SDA.Pin_1, 4_7k_SCL.Pin_1
  GND: U1.GND, DHT1.GND, Grove1.GND, Grove2.GND, Componente1.GND, S3.L1, U2.E, U3.-, U4.-, U5.-, 10k_FRIO.Pin_1, NPN_FRIO.emitter, 100nF_SSR_FRIO.1, 10k_CALOR.Pin_1, NPN_CALOR.emitter, 100nF_SSR_CALOR.1, 10k_VENT.Pin_1, NPN_VENT.emitter, 100nF_SSR_VENT.1, 100nF_ESP8266.1, 100nF_OLED_A.1, 100nF_OLED_B.1, 100nF_RTC.1, 100nF_DHT22.1, 100uF_bulk_3V3.-
  N6: U1.D5, DHT1.DATA
  N7: U1.D6, 1k_VENT.Pin_0
  N8: U1.D7, 1k_FRIO.Pin_0
  N9: U1.D8, 1k_CALOR.Pin_0
  N10: U1.A0, U2.S
  N11: U3.+, NPN_FRIO.collector, 100nF_SSR_FRIO.0
  N12: U4.+, NPN_CALOR.collector, 100nF_SSR_CALOR.0
  N13: U5.+, NPN_VENT.collector, 100nF_SSR_VENT.0
  N14: 1k_FRIO.Pin_1, 10k_FRIO.Pin_0, NPN_FRIO.base
  N15: 1k_CALOR.Pin_1, 10k_CALOR.Pin_0, NPN_CALOR.base
  N16: 1k_VENT.Pin_1, 10k_VENT.Pin_0, NPN_VENT.base

custom parts:
  ESP8266 NodeMCU LoLin module: ESP8266 based NodeMCU
